# Fritzing sketch Untitled Sketch 2 (saved by Fritzing 0.8.7b)
breadboards: 1

parts:
  Part1 = Arduino Uno (Rev3)
  LED1 = LED - 5mm [color="Red (633nm)" package="5 mm [THT]"]
  S1 = Pushbutton [package="[SMD]"]
  R2 = Resistor [tolerance=±5% resistance=10k package=THT]
  S2 = Pushbutton [package="[SMD]"]
  R3 = Resistor [tolerance=±5% resistance=10k package=THT]
  R4 = Trimmer Potentiometer [maximum_resistance=10kΩ package=THT]
  U1 = LCD-16X2 [package=lcd-16x2]
  R5 = Resistor [tolerance=±5% resistance=220 package=THT]

nets (from the schematic view):
  5V: Part1.D8, Part1.D10_PWM/SS, Part1.5V, S1.Pin_3, S1.Pin_4, R2.Pin_0, S2.Pin_1, S2.Pin_2, R3.Pin_0, R4.wiper, U1.VDD, U1.A
  N1: Part1.D9_PWM, R5.Pin_0
  N2: Part1.D1/TX, U1.RS
  N3: Part1.D2, U1.E
  N4: Part1.D4, U1.DB4
  N5: Part1.D5_PWM, U1.DB5
  N6: Part1.D6_PWM, U1.DB6
  N7: Part1.D7, U1.DB7
  GND: Part1.GND, LED1.anode, R2.Pin_1, R3.Pin_1, U1.VSS, U1.R_W, U1.K
  N8: LED1.cathode, R5.Pin_1
  N9: S1.Pin_1, S1.Pin_2
  N10: S2.Pin_3, S2.Pin_4
  N11: R4.leg2, U1.VO
